# Fritzing sketch CircuitDiagram (saved by Fritzing 0.9.3b)

parts:
  元件1 = Arduino Uno (Rev3) - ICSP
  元件2 = Thumb Joystick
  元件3 = Thumb Joystick

nets:
  N1: 元件1.A0, 元件3.SEL
  N2: 元件1.A1, 元件3.HORZ
  N3: 元件1.A2, 元件2.SEL
  N4: 元件1.A3, 元件2.HORZ
  N5: 元件1.D12/MISO, 元件3.GND
  N6: 元件1.D13/SCK, 元件2.GND
